# Fritzing sketch Water-meter gen2 (saved by Fritzing 1.0.6)
circuit board: 4.18066cm x 3.60115cm
breadboards: 1

parts:
  R1 = Resistor [tolerance=±5% resistance=10k package="1206 [SMD]"]
  R2 = Resistor [tolerance=±5% resistance=10k package="1206 [SMD]"]
  R3 = Resistor [tolerance=±5% resistance=10k package="1206 [SMD]"]
  L = JST XH 2A male [form="♂ (male)" package=THT]
  M2 = JST XH 3A Male [chip_label=? package=THT]
  M1 = JST XH 3A Male [chip_label=? package=THT]
  M4 = DOIT Esp32 DevKit v1 (30 pins long, 11 pins width) [part_number=ESP32S-PIN30]

nets:
  N1: R1.Pin_0, R2.Pin_0, M4.3V3
  N2: R1.Pin_1, M2.pin3, M4.D18
  N3: R2.Pin_1, M1.pin3, M4.D19
  N4: R3.Pin_0, L.pin1
  N5: R3.Pin_1, M4.D21
  N6: L.pin2, M2.pin1, M1.pin1, M4.GND
  N7: M2.pin2, M1.pin2, M4.VIN

notes:
  ANMA Water Meter Gen2

custom parts:
  JST XH 2A male: JST XH-2A
  JST XH 3A Male: 2.54 Mm JST "XH" connector
  DOIT Esp32 DevKit v1 (30 pins long, 11 pins width): The DOIT Esp32 DevKit v1 is one of the development board created by DOIT to evaluate the ESP-WROOM-32 module. It is based on the ESP32 microcontroller that boasts Wifi, Bluetooth, Ethernet and Low Power support all in a single chip. (vanepp) made breadboard work, adjusted pin numbering and labels and reduced size of schematic and cleaned up pcb. This chip is 30pins long (2 x15) and 11 pins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
